// Logisim project ALU.circ as structural Verilog: 1 circuit, main circuit main
module main (
  input  [3:0] A,
  input  [3:0] B,
  input  [3:0] OP,
  output [3:0] out_4
);

  wire [3:0] and_1_out, and_2_out, and_3_out, nand_1_out, nor_1_out, not_1_out, not_2_out, or_1_out,
       or_2_out, or_3_out, xnor_1_out, xor_1_out;

  assign not_1_out = ~A;  // NOT_Gate not_1, 4 bits wide
  assign not_2_out = ~B;  // NOT_Gate not_2, 4 bits wide
  assign nor_1_out = ~(B | A);  // NOR_Gate nor_1, 4 bits wide
  assign and_1_out = B & not_1_out;  // AND_Gate and_1, 4 bits wide
  assign nand_1_out = ~(B & A);  // NAND_Gate nand_1, 4 bits wide
  assign xor_1_out = B ^ A;  // XOR_Gate xor_1, 4 bits wide
  assign and_2_out = not_2_out & A;  // AND_Gate and_2, 4 bits wide
  assign or_1_out = B | not_1_out;  // OR_Gate or_1, 4 bits wide
  assign xnor_1_out = ~(B ^ A);  // XNOR_Gate xnor_1, 4 bits wide
  assign and_3_out = B & A;  // AND_Gate and_3, 4 bits wide
  assign or_2_out = not_2_out | A;  // OR_Gate or_2, 4 bits wide
  assign or_3_out = B | A;  // OR_Gate or_3, 4 bits wide
  Multiplexer #(.select(4), .width(4)) multiplexer_1 (
    .in0(not_1_out), .in1(nor_1_out), .in2(and_1_out), .in3(4'b0000), .in4(nand_1_out), .in5(not_2_out),
    .in6(xor_1_out), .in7(and_2_out), .in8(or_1_out), .in9(xnor_1_out), .in10(B), .in11(and_3_out),
    .in12(4'b1111), .in13(or_2_out), .in14(or_3_out), .in15(A), .out(out_4), .sel(OP), .en(1'b1));
endmodule
