// Logisim project CLA_7Display.circ as structural Verilog: 3 circuits, main circuit main
module main (
  input  [3:0] a,
  input  [3:0] a_2
);

  wire cla_1_s1, cla_1_s2, cla_1_s3, cla_1_s4, decodificador_1_s, decodificador_1_u, decodificador_1_v,
       decodificador_1_w, decodificador_1_x, decodificador_1_y, decodificador_1_z, decodificador_2_s,
       decodificador_2_u, decodificador_2_v, decodificador_2_w, decodificador_2_x, decodificador_2_y,
       decodificador_2_z, decodificador_3_s, decodificador_3_u, decodificador_3_v, decodificador_3_w,
       decodificador_3_x, decodificador_3_y, decodificador_3_z;

  Decodificador decodificador_1 (
    .a(a[3]), .b(a[2]), .c(a[1]), .d(a[0]), .x(decodificador_1_x), .y(decodificador_1_y),
    .z(decodificador_1_z), .u(decodificador_1_u), .v(decodificador_1_v), .w(decodificador_1_w),
    .s(decodificador_1_s));
  CLA cla_1 (
    .B4(a[3]), .A4(a_2[3]), .B3(a[2]), .A3(a_2[2]), .B2(a[1]), .A2(a_2[1]), .B1(a[0]), .A1(a_2[0]),
    .in_9(1'b0), .S4(cla_1_s4), .S3(cla_1_s3), .S2(cla_1_s2), .S1(cla_1_s1));  // open: C4
  Decodificador decodificador_2 (
    .a(a_2[3]), .b(a_2[2]), .c(a_2[1]), .d(a_2[0]), .x(decodificador_2_x), .y(decodificador_2_y),
    .z(decodificador_2_z), .u(decodificador_2_u), .v(decodificador_2_v), .w(decodificador_2_w),
    .s(decodificador_2_s));
  Decodificador decodificador_3 (
    .a(cla_1_s4), .b(cla_1_s3), .c(cla_1_s2), .d(cla_1_s1), .x(decodificador_3_x), .y(decodificador_3_y),
    .z(decodificador_3_z), .u(decodificador_3_u), .v(decodificador_3_v), .w(decodificador_3_w),
    .s(decodificador_3_s));
  _7_Segment_Display u_7_segment_display_1 (
    .g(decodificador_1_s), .f(decodificador_1_w), .a(decodificador_1_x), .b(decodificador_1_y),
    .e(decodificador_1_v), .d(decodificador_1_u), .c(decodificador_1_z));  // open: dp
  _7_Segment_Display u_7_segment_display_2 (
    .g(decodificador_2_s), .f(decodificador_2_w), .a(decodificador_2_x), .b(decodificador_2_y),
    .e(decodificador_2_v), .d(decodificador_2_u), .c(decodificador_2_z));  // open: dp
  _7_Segment_Display u_7_segment_display_3 (
    .g(decodificador_3_s), .f(decodificador_3_w), .a(decodificador_3_x), .b(decodificador_3_y),
    .e(decodificador_3_v), .d(decodificador_3_u), .c(decodificador_3_z));  // open: dp
endmodule

module Decodificador (
  input  a,
  input  b,
  input  c,
  input  d,
  output x,
  output y,
  output z,
  output u,
  output v,
  output w,
  output s
);

  wire and_1_out, and_2_out, and_3_out, and_4_out, and_5_out, and_6_out, and_7_out, and_8_out, and_9_out,
       and_10_out, and_11_out, and_12_out, and_13_out, and_14_out, and_15_out, and_16_out, and_17_out,
       and_18_out, and_19_out, and_20_out, and_21_out, and_22_out, and_23_out, and_24_out, and_25_out,
       and_26_out, and_27_out, and_28_out, and_29_out, and_30_out, and_31_out, and_32_out, and_33_out,
       and_34_out, and_35_out, not_1_out, not_2_out, not_3_out, not_4_out, not_5_out, not_6_out, not_7_out,
       not_8_out, not_9_out, not_10_out, not_11_out, not_12_out, not_13_out, not_14_out, not_15_out,
       not_16_out, not_17_out, not_18_out, not_19_out, not_20_out, not_21_out, not_22_out, not_23_out,
       not_24_out, not_25_out, not_26_out, not_27_out, not_28_out, not_29_out, not_30_out, not_31_out,
       not_32_out, not_33_out, not_34_out, not_35_out, not_36_out, not_37_out, not_38_out, not_39_out,
       not_40_out, not_41_out, not_42_out, not_43_out;

  not not_1 (not_1_out, b);
  and and_1 (and_1_out, not_1_out, not_2_out);
  not not_2 (not_2_out, d);
  not not_3 (not_3_out, a);
  and and_2 (and_2_out, not_3_out, c);
  not not_4 (not_4_out, a);
  and and_3 (and_3_out, not_4_out, b, d);
  and and_4 (and_4_out, b, c);
  and and_5 (and_5_out, a, not_5_out, not_6_out);
  not not_5 (not_5_out, b);
  not not_6 (not_6_out, c);
  and and_6 (and_6_out, a, not_7_out);
  not not_7 (not_7_out, d);
  not not_8 (not_8_out, a);
  and and_7 (and_7_out, not_8_out, not_9_out);
  not not_9 (not_9_out, b);
  not not_10 (not_10_out, a);
  not not_11 (not_11_out, c);
  and and_8 (and_8_out, not_10_out, not_11_out, not_12_out);
  not not_12 (not_12_out, d);
  not not_13 (not_13_out, b);
  and and_9 (and_9_out, not_13_out, not_14_out);
  not not_14 (not_14_out, d);
  not not_15 (not_15_out, a);
  and and_10 (and_10_out, not_15_out, c, d);
  and and_11 (and_11_out, a, not_16_out, d);
  not not_16 (not_16_out, c);
  not not_17 (not_17_out, a);
  and and_12 (and_12_out, not_17_out, not_18_out);
  not not_18 (not_18_out, c);
  not not_19 (not_19_out, a);
  and and_13 (and_13_out, not_19_out, d);
  not not_20 (not_20_out, c);
  and and_14 (and_14_out, not_20_out, d);
  not not_21 (not_21_out, a);
  and and_15 (and_15_out, not_21_out, b);
  and and_16 (and_16_out, a, not_22_out);
  not not_22 (not_22_out, b);
  not not_23 (not_23_out, a);
  not not_24 (not_24_out, b);
  and and_17 (and_17_out, not_23_out, not_24_out, not_25_out);
  not not_25 (not_25_out, d);
  not not_26 (not_26_out, b);
  and and_18 (and_18_out, not_26_out, c, d);
  not not_27 (not_27_out, c);
  and and_19 (and_19_out, b, not_27_out, d);
  and and_20 (and_20_out, b, c, not_28_out);
  not not_28 (not_28_out, d);
  and and_21 (and_21_out, a, not_29_out);
  not not_29 (not_29_out, c);
  not not_30 (not_30_out, b);
  and and_22 (and_22_out, not_30_out, not_31_out);
  not not_31 (not_31_out, d);
  and and_23 (and_23_out, c, not_32_out);
  not not_32 (not_32_out, d);
  and and_24 (and_24_out, a, c);
  and and_25 (and_25_out, a, b);
  not not_33 (not_33_out, c);
  and and_26 (and_26_out, not_33_out, not_34_out);
  not not_34 (not_34_out, d);
  not not_35 (not_35_out, a);
  and and_27 (and_27_out, not_35_out, b, not_36_out);
  not not_36 (not_36_out, c);
  and and_28 (and_28_out, b, not_37_out);
  not not_37 (not_37_out, d);
  and and_29 (and_29_out, a, not_38_out);
  not not_38 (not_38_out, b);
  and and_30 (and_30_out, a, c);
  not not_39 (not_39_out, b);
  and and_31 (and_31_out, not_39_out, c);
  and and_32 (and_32_out, c, not_40_out);
  not not_40 (not_40_out, d);
  not not_41 (not_41_out, a);
  and and_33 (and_33_out, not_41_out, b, not_42_out);
  not not_42 (not_42_out, c);
  and and_34 (and_34_out, a, not_43_out);
  not not_43 (not_43_out, b);
  and and_35 (and_35_out, a, d);
  or or_1 (y, and_7_out, and_8_out, and_9_out, and_10_out, and_11_out);
  or or_2 (z, and_12_out, and_13_out, and_14_out, and_15_out, and_16_out);
  or or_3 (u, and_17_out, and_18_out, and_19_out, and_20_out, and_21_out);
  or or_4 (v, and_22_out, and_23_out, and_24_out, and_25_out);
  or or_5 (w, and_26_out, and_27_out, and_28_out, and_29_out, and_30_out);
  or or_6 (s, and_31_out, and_32_out, and_33_out, and_34_out, and_35_out);
  or or_7 (x, and_1_out, and_2_out, and_3_out, and_4_out, and_5_out, and_6_out);
endmodule

module CLA (
  input  B4,
  input  A4,
  input  B3,
  input  A3,
  input  B2,
  input  A2,
  input  B1,
  input  A1,
  input  in_9,
  output C4,
  output S4,
  output S3,
  output S2,
  output S1
);

  wire nand_1_out, nand_2_out, nand_3_out, nand_4_out, nand_5_out, nand_6_out, nand_7_out, nand_8_out,
       nand_9_out, nand_10_out, nand_11_out, nand_12_out, nand_13_out, nand_14_out, nand_15_out, nand_16_out,
       nand_17_out, nand_18_out, nand_19_out, nand_20_out, nand_21_out, nand_22_out, nand_23_out,
       nand_24_out, nand_25_out, nand_26_out, nand_27_out, nand_28_out, nand_29_out, nand_30_out,
       nand_31_out, nand_32_out, nand_33_out, nand_34_out, nor_1_out, nor_2_out, nor_3_out, nor_4_out,
       not_1_out, not_2_out, not_3_out, not_4_out, not_5_out, not_6_out, not_7_out, not_8_out, not_9_out,
       not_10_out, not_11_out, not_12_out, not_13_out, not_14_out, not_15_out, not_16_out, not_17_out,
       not_18_out, not_19_out, not_20_out, not_21_out, not_22_out, not_23_out, not_24_out, not_25_out,
       not_26_out, not_27_out, not_28_out, not_29_out, not_30_out, not_32_out, not_33_out, not_34_out,
       not_35_out, not_36_out;

  not not_1 (not_1_out, B4);
  not not_2 (not_2_out, A4);
  not not_3 (not_3_out, B3);
  not not_4 (not_4_out, A3);
  not not_5 (not_5_out, B2);
  not not_6 (not_6_out, A2);
  not not_7 (not_7_out, B1);
  not not_8 (not_8_out, A1);
  nor nor_1 (nor_1_out, not_1_out, not_2_out);
  nand nand_1 (nand_1_out, not_1_out, not_2_out);
  nor nor_2 (nor_2_out, not_3_out, not_4_out);
  nand nand_2 (nand_2_out, not_3_out, not_4_out);
  not not_9 (not_9_out, nand_2_out);
  nor nor_3 (nor_3_out, not_5_out, not_6_out);
  not not_10 (not_10_out, nor_3_out);
  not not_11 (not_11_out, nand_3_out);
  nand nand_3 (nand_3_out, not_5_out, not_6_out);
  not not_12 (not_12_out, nor_4_out);
  nor nor_4 (nor_4_out, not_7_out, not_8_out);
  nand nand_4 (nand_4_out, not_7_out, not_8_out);
  not not_13 (not_13_out, nand_4_out);
  not not_14 (not_14_out, nor_1_out);
  not not_15 (not_15_out, nand_1_out);
  not not_16 (not_16_out, nor_2_out);
  not not_17 (not_17_out, in_9);
  not not_18 (not_18_out, not_15_out);
  not not_19 (not_19_out, not_9_out);
  not not_20 (not_20_out, not_11_out);
  not not_21 (not_21_out, not_13_out);
  not not_22 (not_22_out, not_15_out);
  nand nand_5 (nand_5_out, not_9_out, not_14_out);
  nand nand_6 (nand_6_out, not_11_out, not_14_out, not_16_out);
  nand nand_7 (nand_7_out, not_13_out, not_14_out, not_16_out, not_10_out);
  nand nand_8 (nand_8_out, not_14_out, not_16_out, not_10_out, not_12_out, not_17_out);
  nand nand_9 (nand_9_out, not_14_out, not_18_out);
  not not_23 (not_23_out, not_9_out);
  nand nand_10 (nand_10_out, not_11_out, not_16_out);
  nand nand_11 (nand_11_out, not_13_out, not_16_out, not_10_out);
  nand nand_12 (nand_12_out, not_16_out, not_10_out, not_12_out, not_17_out);
  nand nand_13 (nand_13_out, not_16_out, not_19_out);
  not not_24 (not_24_out, not_11_out);
  nand nand_14 (nand_14_out, not_13_out, not_10_out);
  nand nand_15 (nand_15_out, not_10_out, not_12_out, not_17_out);
  nand nand_16 (nand_16_out, not_10_out, not_20_out);
  not not_25 (not_25_out, not_13_out);
  nand nand_17 (nand_17_out, not_12_out, not_17_out);
  nand nand_18 (nand_18_out, not_12_out, not_21_out);
  nand nand_19 (nand_19_out, not_22_out, nand_5_out, nand_6_out, nand_7_out, nand_8_out);
  nand nand_20 (nand_20_out, not_23_out, nand_10_out, nand_11_out, nand_12_out);
  nand nand_21 (nand_21_out, not_24_out, nand_14_out, nand_15_out);
  nand nand_22 (nand_22_out, not_25_out, nand_17_out);
  not not_26 (not_26_out, not_27_out);
  not not_27 (not_27_out, nand_19_out);
  not not_28 (not_28_out, nand_9_out);
  not not_29 (not_29_out, nand_20_out);
  not not_30 (not_30_out, nand_21_out);
  not not_31 (C4, not_26_out);
  nand nand_23 (nand_23_out, not_28_out, not_29_out);
  nand nand_24 (nand_24_out, nand_9_out, nand_20_out);
  not not_32 (not_32_out, nand_13_out);
  nand nand_25 (nand_25_out, not_32_out, not_30_out);
  nand nand_26 (nand_26_out, nand_13_out, nand_21_out);
  not not_33 (not_33_out, nand_16_out);
  nand nand_27 (nand_27_out, not_33_out, not_34_out);
  not not_34 (not_34_out, nand_22_out);
  nand nand_28 (nand_28_out, nand_16_out, nand_22_out);
  not not_35 (not_35_out, nand_18_out);
  not not_36 (not_36_out, not_17_out);
  nand nand_29 (nand_29_out, nand_23_out, nand_24_out);
  not not_37 (S4, nand_29_out);
  nand nand_30 (nand_30_out, nand_25_out, nand_26_out);
  nand nand_31 (nand_31_out, nand_27_out, nand_28_out);
  nand nand_32 (nand_32_out, not_35_out, not_36_out);
  nand nand_33 (nand_33_out, nand_32_out, nand_34_out);
  nand nand_34 (nand_34_out, nand_18_out, not_17_out);
  not not_38 (S3, nand_30_out);
  not not_39 (S2, nand_31_out);
  not not_40 (S1, nand_33_out);
endmodule
