// Logisim project Demultiplexador.circ as structural Verilog: 2 circuits, main circuit main
module main (
  input  in_1,
  input  in_2,
  input  in_3,
  input  in_4,
  input  in_5
);

  wire and_2_out, nand_1_out, nor_1_out, or_1_out, somador_1_out_3, somador_1_out_4, xnor_1_out, xor_1_out;

  Somador somador_1 (.in_1(in_1), .in_2(in_2), .out_3(somador_1_out_3), .out_4(somador_1_out_4));
  // AND_Gate and_1 has open pins: in0=in_3, in1=in_4, in2=somador_1_out_4, in3=in_5, out=open
  and and_2 (and_2_out, in_1, in_2);
  // AND_Gate and_3 has open pins: in0=in_3, in1=in_4, in2=and_2_out, in3=in_5, out=open
  nand nand_1 (nand_1_out, in_1, in_2);
  // AND_Gate and_4 has open pins: in0=in_3, in1=in_3, in2=nand_1_out, in3=in_5, out=open
  or or_1 (or_1_out, in_1, in_2);
  // AND_Gate and_5 has open pins: in0=in_3, in1=in_4, in2=or_1_out, in3=in_5, out=open
  nor nor_1 (nor_1_out, in_1, in_2);
  // AND_Gate and_6 has open pins: in0=in_3, in1=in_4, in2=nor_1_out, in3=in_5, out=open
  xor xor_1 (xor_1_out, in_1, in_2);
  // AND_Gate and_7 has open pins: in0=in_3, in1=in_4, in2=xor_1_out, in3=in_5, out=open
  xnor xnor_1 (xnor_1_out, in_1, in_2);
  // AND_Gate and_8 has open pins: in0=in_3, in1=in_4, in2=xnor_1_out, in3=in_5, out=open
endmodule

module Somador (
  input  in_1,
  input  in_2,
  output out_3,
  output out_4
);

  and and_1 (out_3, in_2, in_1);
  xor xor_1 (out_4, in_1, in_2);
endmodule
