// Logisim project MeioSomador_1bit.circ as structural Verilog: 1 circuit, main circuit main
module main (
  input  A0,
  input  B0,
  input  A0_2,
  input  B0_2,
  output S0,
  output CO,
  output S0_2,
  output CO_2
);

  wire and_2_out, and_3_out, not_1_out, not_2_out;

  xor xor_1 (S0, A0, B0);
  and and_1 (CO, A0, B0);
  not not_1 (not_1_out, A0_2);
  not not_2 (not_2_out, B0_2);
  and and_2 (and_2_out, not_1_out, B0_2);
  and and_3 (and_3_out, A0_2, not_2_out);
  or or_1 (S0_2, and_2_out, and_3_out);
  and and_4 (CO_2, A0_2, B0_2);
endmodule
