// Logisim project Multiplexador.circ as structural Verilog: 3 circuits, main circuit main
module main (
  input  in_1,
  input  in_2,
  input  in_3,
  input  in_4,
  input  in_5,
  output out_6
);

  Multiplexer multiplexer_1 (.in_1(in_1), .in_2(in_2), .out_6(out_6), .in_3(in_3), .in_4(in_4), .in_5(in_5));

  // Notes on the sheet:
  //   100 ----- +
  //   010 ----- AND
  //   110 ----- NAND
  //   001 ----- OR
  //   101 ----- NOR
  //   011 ----- XOR
  //   111 ----- XNOR
endmodule

module Somador (
  input  in_1,
  input  in_2,
  output out_3,
  output out_4
);

  and and_1 (out_3, in_2, in_1);
  xor xor_1 (out_4, in_1, in_2);
endmodule

module Multiplexer (
  input  in_1,
  input  in_2,
  input  in_3,
  input  in_4,
  input  in_5,
  output out_6
);

  wire and_1_out, and_2_out, and_3_out, and_4_out, and_5_out, and_6_out, and_7_out, and_8_out, nand_1_out,
       nor_1_out, or_1_out, somador_1_out_4, xnor_1_out, xor_1_out;

  Somador somador_1 (.in_1(in_1), .in_2(in_2), .out_4(somador_1_out_4));  // open: out_3
  and and_1 (and_1_out, in_3, ~in_4, somador_1_out_4, ~in_5);  // AND_Gate
  and and_2 (and_2_out, in_1, in_2);
  and and_3 (and_3_out, ~in_3, in_4, and_2_out, ~in_5);  // AND_Gate
  nand nand_1 (nand_1_out, in_1, in_2);
  and and_4 (and_4_out, in_3, in_4, nand_1_out, ~in_5);  // AND_Gate
  or or_1 (or_1_out, in_1, in_2);
  and and_5 (and_5_out, ~in_3, ~in_4, or_1_out, in_5);  // AND_Gate
  or or_2 (out_6, and_1_out, and_3_out, and_4_out, and_5_out, and_6_out, and_7_out, and_8_out);
  nor nor_1 (nor_1_out, in_1, in_2);
  and and_6 (and_6_out, in_3, ~in_4, nor_1_out, in_5);  // AND_Gate
  xor xor_1 (xor_1_out, in_1, in_2);
  and and_7 (and_7_out, ~in_3, in_4, xor_1_out, in_5);  // AND_Gate
  xnor xnor_1 (xnor_1_out, in_1, in_2);
  and and_8 (and_8_out, in_3, in_4, xnor_1_out, in_5);
endmodule
