// Logisim project Somador.circ as structural Verilog: 2 circuits, main circuit main
module main (
  input  A3,
  input  A2,
  input  A1,
  input  A0,
  input  B3,
  input  B2,
  input  B1,
  input  B0,
  output out_9,
  output out_10,
  output out_11,
  output out_12,
  output out_13
);

  wire somador_1_co, somador_2_co, somador_3_co;

  Somador somador_1 (.A0(A0), .B0(B0), .in_1(1'b0), .CO(somador_1_co), .S0(out_13));
  Somador somador_2 (.A0(A1), .B0(B1), .in_1(somador_1_co), .CO(somador_2_co), .S0(out_12));
  Somador somador_3 (.A0(A2), .B0(B2), .in_1(somador_2_co), .CO(somador_3_co), .S0(out_11));
  Somador somador_4 (.A0(A3), .B0(B3), .in_1(somador_3_co), .CO(out_9), .S0(out_10));
endmodule

module Somador (
  input  in_1,
  input  A0,
  input  B0,
  output S0,
  output CO
);

  wire and_1_out, and_2_out, xor_1_out;

  xor xor_1 (xor_1_out, A0, B0);
  and and_1 (and_1_out, A0, B0);
  xor xor_2 (S0, in_1, xor_1_out);
  and and_2 (and_2_out, in_1, xor_1_out);
  or or_1 (CO, and_2_out, and_1_out);
endmodule
