// Logisim project Somador_Completo_4bits.circ as structural Verilog: 2 circuits, main circuit main
module main (
  input  [3:0] in_1,
  input  [3:0] in_2,
  output out_3,
  output out_4,
  output out_5,
  output out_6,
  output out_7
);

  wire somador_1_co, somador_2_co, somador_3_co;

  Somador somador_1 (.A0(in_1[0]), .B0(in_2[0]), .in_1(1'b0), .CO(somador_1_co), .S0(out_7));
  Somador somador_2 (.A0(in_1[1]), .B0(in_2[1]), .in_1(somador_1_co), .CO(somador_2_co), .S0(out_6));
  Somador somador_3 (.A0(in_1[2]), .B0(in_2[2]), .in_1(somador_2_co), .CO(somador_3_co), .S0(out_5));
  Somador somador_4 (.A0(in_1[3]), .B0(in_2[3]), .in_1(somador_3_co), .CO(out_3), .S0(out_4));
endmodule

module Somador (
  input  in_1,
  input  A0,
  input  B0,
  output S0,
  output CO
);

  wire and_1_out, and_2_out, xor_1_out;

  xor xor_1 (xor_1_out, A0, B0);
  and and_1 (and_1_out, A0, B0);
  xor xor_2 (S0, in_1, xor_1_out);
  and and_2 (and_2_out, in_1, xor_1_out);
  or or_1 (CO, and_2_out, and_1_out);
endmodule
