// Logisim project ULA.circ as structural Verilog: 5 circuits, main circuit main
module main (
  input  [3:0] in_1,
  input  [3:0] in_2,
  input  C_in___Binversor,
  input  [1:0] in_4,
  output [3:0] out_5,
  output Tudo_Zero,
  output Negativo,
  output C_out
);

  Ula_4bits ula_4bits_1 (
    .A0(in_1[0]), .B0(in_2[0]), .A1(in_1[1]), .B1(in_2[1]), .A2(in_1[2]), .B2(in_2[2]), .A3(in_1[3]),
    .B3(in_2[3]), .in_10(in_4), .out_17(C_out), .in_1(C_in___Binversor), ._2_0(out_5[0]), .out_12(out_5[1]),
    .out_13(out_5[2]), ._2_3(out_5[3]), .Tudo_zero(Tudo_Zero), .\É_negativo (Negativo));
endmodule

module Somador (
  input  C_in,
  input  A,
  input  B,
  output S,
  output C_out
);

  wire and_1_out, and_2_out, xor_1_out;

  xor xor_1 (xor_1_out, A, B);
  and and_1 (and_1_out, A, B);
  xor xor_2 (S, C_in, xor_1_out);
  and and_2 (and_2_out, C_in, xor_1_out);
  or or_1 (C_out, and_1_out, and_2_out);
endmodule

module Multiplexador (
  input  in_1,
  input  in_2,
  input  in_3,
  input  in_4,
  input  Op1,
  input  Op0,
  output S
);

  wire and_1_out, and_2_out, and_3_out, and_4_out, and_5_out, and_6_out, and_7_out, and_8_out, not_1_out,
       not_2_out, not_3_out, not_4_out, or_1_out, or_2_out;

  and and_1 (and_1_out, in_1, not_1_out);
  not not_1 (not_1_out, Op0);
  not not_2 (not_2_out, Op1);
  not not_3 (not_3_out, Op1);
  not not_4 (not_4_out, Op0);
  and and_2 (and_2_out, and_1_out, not_2_out);
  and and_3 (and_3_out, in_2, not_3_out);
  and and_4 (and_4_out, and_3_out, Op0);
  and and_5 (and_5_out, in_3, Op1);
  and and_6 (and_6_out, and_5_out, not_4_out);
  and and_7 (and_7_out, in_4, Op1);
  and and_8 (and_8_out, and_7_out, Op0);
  or or_1 (or_1_out, and_2_out, and_4_out);
  or or_2 (or_2_out, and_6_out, and_8_out);
  or or_3 (S, or_1_out, or_2_out);
endmodule

module ULA (
  input  Binversor,
  input  in_2,
  input  A,
  input  B,
  input  Op1,
  input  Op0,
  output S,
  output C_Out
);

  wire and_1_out, multiplexer_1_out, not_1_out, not_2_out, or_1_out, somador_1_s;

  not not_1 (not_1_out, B);
  Multiplexer #(.enable("false")) multiplexer_1 (.in0(B), .in1(not_1_out), .out(multiplexer_1_out), .sel(Binversor));
  and and_1 (and_1_out, A, B);
  or or_1 (or_1_out, A, B);
  not not_2 (not_2_out, A);
  Somador somador_1 (.A(A), .B(multiplexer_1_out), .C_in(in_2), .C_out(C_Out), .S(somador_1_s));
  Multiplexador multiplexador_1 (
    .in_1(and_1_out), .in_2(or_1_out), .in_3(not_2_out), .in_4(somador_1_s), .Op1(Op1), .Op0(Op0), .S(S));
endmodule

module Ula_4bits (
  input  in_1,
  input  A0,
  input  B0,
  input  A1,
  input  B1,
  input  A2,
  input  B2,
  input  A3,
  input  B3,
  input  [1:0] in_10,
  output _2_0,
  output out_12,
  output out_13,
  output _2_3,
  output Tudo_zero,
  output \É_negativo ,
  output out_17
);

  wire ula_1_c_out, ula_2_c_out, ula_3_c_out;

  ULA ula_1 (
    .A(A0), .B(B0), .Binversor(in_1), .in_2(in_1), .C_Out(ula_1_c_out), .Op1(in_10[1]), .Op0(in_10[0]),
    .S(_2_0));
  ULA ula_2 (
    .A(A1), .B(B1), .Binversor(in_1), .in_2(ula_1_c_out), .C_Out(ula_2_c_out), .Op1(in_10[1]),
    .Op0(in_10[0]), .S(out_12));
  ULA ula_3 (
    .A(A2), .B(B2), .Binversor(in_1), .in_2(ula_2_c_out), .C_Out(ula_3_c_out), .Op1(in_10[1]),
    .Op0(in_10[0]), .S(out_13));
  ULA ula_4 (
    .A(A3), .B(B3), .Binversor(in_1), .in_2(ula_3_c_out), .C_Out(out_17), .Op1(in_10[1]), .Op0(in_10[0]),
    .S(_2_3));
  nor nor_1 (Tudo_zero, _2_0, out_12, out_13, _2_3);

  assign \É_negativo  = out_13;

  // Notes on the sheet:
  //   00 -  AND /   01 - OR / 10 - NOT A / 11 - Soma
endmodule
